# Fritzing sketch schem (saved by Fritzing 0.9.3b)
breadboards: 1

parts:
  M1 = DC Motor
  Part1 = Adafruit Feather HUZZAH ESP8266 [part_number="Adafruit #2821"]
  JACK1 = 2.1mm Barrel Jack with Terminal Block
  Part2 = Adafruit TB6612 DC and Stepper Motor Driver [part_number="Adafruit #2448"]

nets:
  N1: M1.pin_1, Part2.MOTORA2
  N2: M1.pin_2, Part2.MOTORA1
  N3: Part1.GND, JACK1.NEG

custom parts:
  Adafruit Feather HUZZAH ESP8266: his is the Adafruit Feather HUZZAH ESP8266 - our take on an 'all-in-one' ESP8266 WiFi development board with built in USB and battery charging. Its an ESP8266 WiFi module with all the extras you need, ready to rock! We have other boards in the Feather family, check'em out here. At the Feather HUZZAH's heart is an ESP8266 WiFi microcontroller clocked at 80 MHz and at 3.3V logic. This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
  Adafruit TB6612 DC and Stepper Motor Driver: Spin two DC motors, step one bi-polar or uni-polar stepper, or fire off two solenoids with 1.2A per channel using the TB6612. These are perhaps better known as "the drivers in our assembled Adafruit Motorshield or Motor HAT." We really like these dual H-bridges, so if you want to control motors without a shield or HAT these are easy to include on any solderless breadboard or perma-proto.
